# Fritzing sketch Laser Kite (saved by Fritzing 0.7.5b)
breadboards: 1

parts:
  R1 = Resistor [tolerance=±5% resistance=220 package=THT]
  C1 = Ceramic Capacitor [capacitance=100nF package="100 mil [THT, multilayer]"]
  IR_Reciever_(TSOP22)1 = IR Reciever
  VCC1 = Battery block 9V
  S1 = Toggle Switch [package=THT]
  Part1 = Pro Trinket 5V

nets:
  N1: R1.Pin_0, C1.0, IR_Reciever_(TSOP22)1.Vs
  N2: R1.Pin_1, Part1.+5V
  GND: C1.1, IR_Reciever_(TSOP22)1.GND, VCC1.-, Part1.GND
  N3: IR_Reciever_(TSOP22)1.OUT, Part1.A0
  N4: VCC1.+, S1.L1
  N5: S1.COM, Part1.VBAT

custom parts:
  IR Reciever: Basic infrared reciever
  Pro Trinket 5V: The Pro Trinket 5V is like an Arduino Pro Mini with more pins and USB included. Built with the common core Arduino chip, the ATmega328p, it has 18 GPIO, 2 extra analog inputs, 28K of flash, and 2K of RAM. It has onboard USB bootloading support with Optiboot support, so you can either program your Pro Trinket over USB or with a FTDI cable. The Pro Trinket is programmable using the Arduino IDE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
