# Fritzing sketch Laser Kite2 (saved by Fritzing 0.7.5b)
breadboards: 1

parts:
  R1 = Resistor [tolerance=±5% resistance=220 package=THT]
  TSOP32438 = 
  VCC = Battery block 9V
  Switch = Toggle Switch [package=THT]
  C1 = Electrolytic Capacitor [capacitance=1µF package="100 mil [THT, electrolytic]"]

nets (from the breadboard view):
  N1: R1.Pin_0, TSOP32438., VCC.-, C1.-
  N2: R1.Pin_1, C1.+
  N3: VCC.+, Switch.L1
