# Fritzing sketch IR Remote (saved by Fritzing 0.7.7b)
breadboards: 1

parts:
  Arduino3 = Arduino
  IC1 = ULN2003A [package="SO16 [SMD]"]
  R1 = Resistor [tolerance=±5% resistance=33 package=THT]
  R2 = Resistor [tolerance=±5% resistance=33 package=THT]
  R3 = Resistor [tolerance=±5% resistance=33 package=THT]
  LED1 = RGB LED (com. anode, rbg) [package="5 mm [THT]"]
  R4 = Resistor [tolerance=±5% resistance=330 package=THT]
  C1 = Electrolytic Capacitor [capacitance=4.7µF package="100 mil [THT, electrolytic]"]
  IR_Reciever_(TSOP22)1 = IR Reciever

nets (from the breadboard view):
  N1: Arduino3.GND, IC1.0V, C1.-, IR_Reciever_(TSOP22)1.OUT
  N2: Arduino3.D11, IC1.In_1
  N3: Arduino3.D9, IC1.In_3
  N4: Arduino3.D8, IR_Reciever_(TSOP22)1.GND
  N5: Arduino3.D6, IC1.In_2
  N6: Arduino3.+5V, LED1.red_cathode, R4.Pin_1
  N7: IC1.Out_3, R1.Pin_1
  N8: IC1.Out_2, R2.Pin_1
  N9: IC1.Out_1, R3.Pin_1
  N10: R1.Pin_0, LED1.common_anode
  N11: R2.Pin_0, LED1.blue_cathode
  N12: R3.Pin_0, LED1.green_cathode
  N13: R4.Pin_0, C1.+, IR_Reciever_(TSOP22)1.Vs

notes:
  TSOP 1736
  GND-VS-OUT

custom parts:
  IR Reciever: Basic infrared reciever
